// Logisim project TD.circ as structural Verilog
module main (
  input  [3:0] in_1,
  input  [1:0] in_2
);

  wire clock_1_out, reg4b_1_sd, reg4b_1_sg;

  Clock clock_1 (.out(clock_1_out));
  reg4b reg4b_1 (.E(in_1), .C(in_2), .H(clock_1_out), .Sg(reg4b_1_sg), .Sd(reg4b_1_sd));
  LED led_1 (.in(reg4b_1_sg));
  LED led_2 (.in(reg4b_1_sd));
endmodule

module encodeur42 (
  input  E0,
  input  E1,
  input  E2,
  input  E3,
  output S0,
  output S1
);

  or or_1 (S0, E1, E3);
  or or_2 (S1, E2, E3);
endmodule

module demiadd1b (
  input  A,
  input  B,
  output S,
  output R
);

  xor xor_1 (S, A, B);
  and and_1 (R, A, B);
endmodule

module decodeur24 (
  input  E1,
  input  E0,
  output S0,
  output S1,
  output S2,
  output S3
);

  wire not_1_out, not_2_out;

  not not_1 (not_1_out, E1);
  not not_2 (not_2_out, E0);
  and and_1 (S0, not_1_out, not_2_out);
  and and_2 (S1, not_1_out, E0);
  and and_3 (S2, E1, not_2_out);
  and and_4 (S3, E1, E0);
endmodule

module fulladd1b (
  input  A,
  input  B,
  input  Re,
  output S,
  output Rs
);

  wire demiadd1b_1_r, demiadd1b_1_s, demiadd1b_2_r;

  demiadd1b demiadd1b_1 (.A(A), .B(B), .S(demiadd1b_1_s), .R(demiadd1b_1_r));
  demiadd1b demiadd1b_2 (.A(demiadd1b_1_s), .B(Re), .S(S), .R(demiadd1b_2_r));
  or or_1 (Rs, demiadd1b_2_r, demiadd1b_1_r);
endmodule

module add4b (
  input  [3:0] B,
  input  Re,
  input  [3:0] A,
  output [3:0] S,
  output Rs
);

  wire fulladd1b_1_rs, fulladd1b_2_rs, fulladd1b_3_rs;

  fulladd1b fulladd1b_1 (.A(A[0]), .B(B[0]), .Re(Re), .S(S[0]), .Rs(fulladd1b_1_rs));
  fulladd1b fulladd1b_2 (.A(A[1]), .B(B[1]), .Re(fulladd1b_1_rs), .S(S[1]), .Rs(fulladd1b_2_rs));
  fulladd1b fulladd1b_3 (.A(A[2]), .B(B[2]), .Re(fulladd1b_2_rs), .S(S[2]), .Rs(fulladd1b_3_rs));
  fulladd1b fulladd1b_4 (.A(A[3]), .B(B[3]), .Re(fulladd1b_3_rs), .S(S[3]), .Rs(Rs));
endmodule

module shifter4b (
  input  [1:0] D,
  input  [3:0] E
);

  Multiplexer #(.select(2)) multiplexer_1 (.in0(E[0]), .in1(E[1]), .in2(E[2]), .in3(E[3]), .sel(D));  // open: out
  Multiplexer #(.select(2)) multiplexer_2 (.in0(E[1]), .in1(E[2]), .in2(E[3]), .in3(E[0]), .sel(D));  // open: out
  Multiplexer #(.select(2)) multiplexer_3 (.in0(E[2]), .in1(E[3]), .in2(E[0]), .in3(E[1]), .sel(D));  // open: out
  Multiplexer #(.select(2)) multiplexer_4 (.in0(E[3]), .in1(E[0]), .in2(E[1]), .in3(E[2]), .sel(D));  // open: out
endmodule

module reg4b (
  input  [3:0] E,
  input  [1:0] C,
  input  H,
  output Sg,
  output Sd
);

  wire d_ff_2_q, d_ff_3_q, multiplexer_1_out, multiplexer_2_out, multiplexer_3_out, multiplexer_4_out;

  Multiplexer #(.select(2)) multiplexer_1 (
    .in0(Sg), .in1(E[3]), .in2(1'b0), .in3(d_ff_2_q), .out(multiplexer_1_out), .sel(C));
  D_Flip_Flop d_ff_1 (.D(multiplexer_1_out), .clk(H), .Q(Sg));  // open: Qn, preset, reset
  Multiplexer #(.select(2)) multiplexer_2 (
    .in0(d_ff_2_q), .in1(E[2]), .in2(Sg), .in3(d_ff_3_q), .out(multiplexer_2_out), .sel(C));
  D_Flip_Flop d_ff_2 (.D(multiplexer_2_out), .clk(H), .Q(d_ff_2_q));  // open: Qn, preset, reset
  Multiplexer #(.select(2)) multiplexer_3 (
    .in0(d_ff_3_q), .in1(E[1]), .in2(d_ff_2_q), .in3(Sd), .out(multiplexer_3_out), .sel(C));
  D_Flip_Flop d_ff_3 (.D(multiplexer_3_out), .clk(H), .Q(d_ff_3_q));  // open: Qn, preset, reset
  Multiplexer #(.select(2)) multiplexer_4 (
    .in0(Sd), .in1(E[0]), .in2(d_ff_3_q), .in3(1'b0), .out(multiplexer_4_out), .sel(C));
  D_Flip_Flop d_ff_4 (.D(multiplexer_4_out), .clk(H), .Q(Sd));  // open: Qn, preset, reset
endmodule

module counter7states (
  input  H
);

  wire and_1_out, and_2_out, and_3_out, D0_q, D1_q, D2_q, not_1_out, not_2_out, or_1_out, or_2_out;

  not not_1 (not_1_out, D2_q);
  not not_2 (not_2_out, D0_q);
  and and_1 (and_1_out, D0_q, D1_q, not_1_out);
  and and_2 (and_2_out, D1_q, not_2_out);
  and and_3 (and_3_out, D2_q, D0_q);
  or or_1 (or_1_out, and_1_out, D2_q);
  or or_2 (or_2_out, and_2_out, and_3_out);
  D_Flip_Flop D0 (.D(D1_q), .clk(H), .Q(D0_q));  // open: Qn, preset, reset
  D_Flip_Flop D1 (.D(or_1_out), .clk(H), .Q(D1_q));  // open: Qn, preset, reset
  D_Flip_Flop D2 (.D(or_2_out), .clk(H), .Q(D2_q));  // open: Qn, preset, reset
endmodule

module alu4b (
  input  [3:0] a,
  input  [3:0] b,
  input  [1:0] c,
  output CC,
  output N,
  output [3:0] r,
  output Z
);

  wire add4b_2_rs, add4b_3_rs;
  wire [3:0] add4b_1_s, add4b_2_s, add4b_3_s, and_1_out, not_1_out;

  assign not_1_out = ~b;  // NOT_Gate not_1, 4 bits wide
  add4b add4b_1 (.B(not_1_out), .A(4'b0001), .S(add4b_1_s));  // open: Re, Rs
  assign and_1_out = a & b;  // AND_Gate and_1, 4 bits wide
  add4b add4b_2 (.B(b), .A(a), .S(add4b_2_s), .Rs(add4b_2_rs));  // open: Re
  add4b add4b_3 (.B(add4b_1_s), .A(a), .S(add4b_3_s), .Rs(add4b_3_rs));  // open: Re
  Multiplexer #(.select(2), .width(4)) multiplexer_1 (
    .in0(add4b_2_s), .in1(add4b_3_s), .in2(and_1_out), .in3(b), .out(r), .sel(c));
  or or_1 (CC, add4b_2_rs, add4b_3_rs);
  and and_2 (N, r[3], 1'b1);
  eq4b eq4b_1 (.A(r), .B(4'b0000), .r(Z));
endmodule

module eq4b (
  input  [3:0] A,
  input  [3:0] B,
  output r
);

  wire not_1_out, not_2_out, not_3_out, not_4_out, xor_1_out, xor_2_out, xor_3_out, xor_4_out;

  xor xor_1 (xor_1_out, A[0], B[0]);
  xor xor_2 (xor_2_out, A[1], B[1]);
  xor xor_3 (xor_3_out, A[2], B[2]);
  xor xor_4 (xor_4_out, A[3], B[3]);
  not not_1 (not_1_out, xor_1_out);
  not not_2 (not_2_out, xor_2_out);
  not not_3 (not_3_out, xor_3_out);
  not not_4 (not_4_out, xor_4_out);
  and and_1 (r, not_1_out, not_2_out, not_3_out, not_4_out);
endmodule

module add1b (
  input  b,
  input  a,
  input  Xe,
  input  Ee,
  output Xs,
  output Rs
);

  wire and_1_out;

  and and_1 (and_1_out, b, a);
  fulladd1b fulladd1b_1 (.A(and_1_out), .B(Xe), .Re(Ee), .S(Xs), .Rs(Rs));
endmodule

module blinkerv1 (
  input  Clk,
  input  C,
  input  Init
);

  wire and_1_out, d_ff_1_q, d_ff_2_q, d_ff_3_q, d_ff_4_q, not_1_out, or_1_out, or_2_out, or_3_out;

  and and_1 (and_1_out, Clk, C);
  not not_1 (not_1_out, C);
  D_Flip_Flop d_ff_1 (.D(d_ff_4_q), .clk(and_1_out), .Q(d_ff_1_q), .preset(or_1_out));  // open: Qn, reset
  or or_1 (or_1_out, Init, not_1_out);
  D_Flip_Flop d_ff_2 (.D(d_ff_1_q), .clk(and_1_out), .Q(d_ff_2_q), .reset(or_1_out));  // open: Qn, preset
  D_Flip_Flop d_ff_3 (.D(d_ff_2_q), .clk(and_1_out), .Q(d_ff_3_q), .reset(or_1_out));  // open: Qn, preset
  D_Flip_Flop d_ff_4 (.D(d_ff_3_q), .clk(and_1_out), .Q(d_ff_4_q), .reset(or_1_out));  // open: Qn, preset
  LED led_1 (.in(d_ff_4_q));
  LED led_2 (.in(or_2_out));
  or or_2 (or_2_out, d_ff_3_q, d_ff_4_q);
  LED led_3 (.in(or_3_out));
  or or_3 (or_3_out, d_ff_2_q, d_ff_3_q, d_ff_4_q);
endmodule

module blinkerv2 (
  input  Clk,
  output [2:0] Q
);

  wire and_1_out, and_2_out, d_ff_1_qn;

  D_Flip_Flop d_ff_1 (.D(and_1_out), .clk(Clk), .Q(Q[2]), .Qn(d_ff_1_qn));  // open: preset, reset
  and and_1 (and_1_out, Q[1], d_ff_1_qn);
  D_Flip_Flop d_ff_2 (.D(and_2_out), .clk(Clk), .Q(Q[1]));  // open: Qn, preset, reset
  and and_2 (and_2_out, d_ff_1_qn, Q[0]);
  D_Flip_Flop d_ff_3 (.D(d_ff_1_qn), .clk(Clk), .Q(Q[0]));  // open: Qn, preset, reset
endmodule

module blinkerv3 (
);

  D_Flip_Flop d_ff_1 ();  // open: D, clk, Q, Qn, preset, reset
  D_Flip_Flop d_ff_2 ();  // open: D, clk, Q, Qn, preset, reset
endmodule

module de_next (
  input  [2:0] Q,
  output [2:0] D
);

  wire and_1_out, and_2_out, and_3_out, and_4_out;

  and and_1 (and_1_out, ~Q[1], Q[2]);  // AND_Gate
  and and_2 (and_2_out, Q[0], Q[1], ~Q[2]);  // AND_Gate
  and and_3 (and_3_out, Q[0], ~Q[1]);  // AND_Gate
  and and_4 (and_4_out, ~Q[0], Q[1], ~Q[2]);  // AND_Gate
  or or_1 (D[2], and_1_out, and_2_out);
  or or_2 (D[1], and_3_out, and_4_out);
  not not_1 (D[0], Q[0]);
endmodule

module de_cpt1a6 (
  input  count,
  input  clk,
  input  init,
  output [2:0] out_4
);

  wire and_1_out;
  wire [2:0] de_next_1_d;

  de_next de_next_1 (.Q(out_4), .D(de_next_1_d));
  D_Flip_Flop D2 (.D(de_next_1_d[2]), .clk(and_1_out), .Q(out_4[2]), .reset(init));  // open: Qn, preset
  D_Flip_Flop D1 (.D(de_next_1_d[1]), .clk(and_1_out), .Q(out_4[1]), .reset(init));  // open: Qn, preset
  D_Flip_Flop D0 (.D(de_next_1_d[0]), .clk(and_1_out), .Q(out_4[0]), .preset(init));  // open: Qn, reset
  and and_1 (and_1_out, count, clk);
endmodule

module cpt1a6 (
  input  in_1
);

  wire button_1_out, clock_1_out, decoder_1_out1, decoder_1_out2, decoder_1_out3, decoder_1_out4,
       decoder_1_out5, decoder_1_out6, or_1_out, or_2_out, or_3_out, or_4_out, or_5_out, or_6_out, or_7_out;
  wire [2:0] de_cpt1a6_1_out_4;

  Button button_1 (.out(button_1_out));
  Clock clock_1 (.out(clock_1_out));
  de_cpt1a6 de_cpt1a6_1 (.count(button_1_out), .clk(clock_1_out), .init(in_1), .out_4(de_cpt1a6_1_out_4));
  Decoder #(.enable("false"), .select(3)) decoder_1 (
    .out1(decoder_1_out1), .out2(decoder_1_out2), .out3(decoder_1_out3), .out4(decoder_1_out4),
    .out5(decoder_1_out5), .out6(decoder_1_out6), .sel(de_cpt1a6_1_out_4));  // open: out0, out7
  or or_1 (or_1_out, decoder_1_out5, decoder_1_out6, decoder_1_out4);
  or or_2 (or_2_out, decoder_1_out2, decoder_1_out6);
  LED led_1 (.in(or_1_out));
  LED led_2 (.in(or_2_out));
  LED led_3 (.in(or_4_out));
  or or_3 (or_3_out, decoder_1_out4, decoder_1_out3, decoder_1_out6, decoder_1_out5);
  LED led_4 (.in(or_3_out));
  or or_4 (or_4_out, decoder_1_out1, decoder_1_out5, decoder_1_out3);
  LED led_5 (.in(or_7_out));
  or or_5 (or_5_out, decoder_1_out6, decoder_1_out2);
  LED led_6 (.in(or_5_out));
  LED led_7 (.in(or_6_out));
  or or_6 (or_6_out, decoder_1_out5, decoder_1_out6, decoder_1_out4);
  or or_7 (or_7_out, decoder_1_out5, decoder_1_out3, decoder_1_out4, decoder_1_out6);
endmodule
