// Logisim project TP.circ as structural Verilog: 3 circuits, main circuit main
module main (
  input  [1:0] b,
  input  [1:0] a
);

  wire not_1_out, not_2_out, not_3_out, not_4_out;

  not not_1 (not_1_out, a[0]);
  not not_2 (not_2_out, b[0]);
  not not_3 (not_3_out, a[1]);
  not not_4 (not_4_out, b[1]);
  LED fA ();  // open: in
  LED fB ();  // open: in
endmodule

module mult4to1 (
  input  i0,
  input  i1,
  input  i2,
  input  i3,
  input  S0,
  input  S1,
  output F
);

  wire multiplexer_1_out, multiplexer_2_out;

  Multiplexer multiplexer_1 (.in0(i0), .in1(i1), .out(multiplexer_1_out), .sel(S0));
  Multiplexer multiplexer_2 (.in0(i2), .in1(i3), .out(multiplexer_2_out), .sel(S0));
  Multiplexer multiplexer_3 (.in0(multiplexer_1_out), .in1(multiplexer_2_out), .out(F), .sel(S1));
endmodule

module mult8to1 (
  input  i0,
  input  i1,
  input  i2,
  input  i3,
  input  S0,
  input  S1,
  input  i4,
  input  S2,
  input  i5,
  input  i6,
  input  i7,
  output F
);

  wire mult4to1_1_f, mult4to1_2_f;

  mult4to1 mult4to1_1 (.i0(i0), .i1(i1), .i2(i2), .i3(i3), .S0(S0), .S1(S1), .F(mult4to1_1_f));
  mult4to1 mult4to1_2 (.i0(i4), .i1(i5), .i2(i6), .i3(i7), .S0(S0), .S1(S1), .F(mult4to1_2_f));
  Multiplexer multiplexer_1 (.in0(mult4to1_1_f), .in1(mult4to1_2_f), .out(F), .sel(S2));
endmodule
